# Fritzing sketch ConexionAlarma2leds (saved by Fritzing 0.9.6b)
breadboards: 1

parts:
  U2 = ESP8266 NodeMCU LoLin module
  LED2 = LEDs [package=led10mm]
  LED3 = LEDs [package=led10mm]

nets:
  N1: U2.D1, LED3.A
  N2: U2.D2, LED2.A
  N3: U2.GND, LED2.C, LED3.C

custom parts:
  ESP8266 NodeMCU LoLin module: ESP8266 based NodeMCU
